# Fritzing sketch Vario2Hott (saved by Fritzing 0.9.3b)

parts:
  J1 = female pin header, 3 pins [form="♀ (female)" part_number=Empfänger]
  R1 = Resistor [tolerance=±0.05% resistance=1.8k package=THT]
  D1 = Zener Diode [part_number="Z-Diode 3,3V" breakdown_voltage=3.3V package="Melf DO-213 AB [SMD]"]
  MS2 = MS5611
  Bauteil1 = Arduino Pro Mini (5V)

nets:
  GND: J1.pin1, D1.anode, MS2.GND, Bauteil1.GND
  N1: J1.pin2, Bauteil1.RAW
  N2: J1.pin3, R1.Pin_0, D1.cathode
  N3: R1.Pin_1, Bauteil1.D3
  VIN: MS2.VIN, Bauteil1.VCC
  N4: MS2.SCL, Bauteil1.A5
  N5: MS2.SDA, Bauteil1.A4

notes:
  -
  +
  T
  Vario2Hott
